// Digital circuit tom-1.dig as structural Verilog
module tom_1 (
  input  clk,
  input  in_2,
  input  [7:0] in_3,
  input  in_4,
  input  in_5,
  input  in_6,
  input  in_7,
  input  [7:0] in_8,
  input  in_9,
  input  in_10,
  input  in_11,
  input  in_12,
  input  in_13,
  input  in_16,
  input  in_17,
  input  in_18,
  output pulse,
  output clk_2
);

  wire d_ff_1_nq, delay_1_out, nclk, not_3_out, not_4_out, not_5_out, not_6_out, not_7_out, npulse,
       nTOS_eq__eq_0_nis0;
  wire [7:0] CTRL_p3, D_REGISTER_q, I_O_HIGH_p3, I_O_LOW_p3, ROM_d, ROM_d_2;
  wire [15:0] NAND_out, PROGRAM_COUNTER_pc, TOS_HIGH_out;

  tom_1_pc PROGRAM_COUNTER (.clk(npulse), .\input ({16{1'b0}}), .nLOAD(in_18), .pc(PROGRAM_COUNTER_pc));
  // Probe PC on PROGRAM_COUNTER_pc
  not not_1 (npulse, clk);
  EEPROM #(.AddrBits(16), .Bits(16)) ROM (
    .A(PROGRAM_COUNTER_pc), .CS(1'b1), .WE(1'b0), .OE(1'b1), .D({ROM_d_2, ROM_d}));
  // Probe ROM on {ROM_d_2, ROM_d}
  LED led_1 (.in(npulse));
  // Probe on npulse
  LED led_2 (.in(clk));
  D_FF d_ff_1 (.D(d_ff_1_nq), .C(npulse), .Q(nclk), .nQ(d_ff_1_nq));
  SixteenSeg sixteenseg_1 (.led({ROM_d_2, ROM_d}), .dp(in_2));
  Delay delay_1 (.in(nclk), .out(delay_1_out));
  not not_2 (clk_2, nclk);
  LED led_3 (.in(clk_2));
  LED led_4 (.in(nclk));
  // tom_1_ctrl CTRL: pin names not known; wires that end beside it: delay_1_out, ROM_d, CTRL_p3
  // Probe CTRL on CTRL_p3
  Break BREAK (.brk(CTRL_p3[7]));
  not not_3 (not_3_out, CTRL_p3[2]);
  not not_4 (not_4_out, CTRL_p3[1]);
  not not_5 (not_5_out, CTRL_p3[0]);
  not not_6 (not_6_out, CTRL_p3[3]);
  tom_1_273 TOS_LOW (.nCLR(in_18), .DATA(ROM_d), .CLK(nclk), .OUT(TOS_HIGH_out[7:0]));
  tom_1_273 TOS_HIGH (.nCLR(in_18), .DATA(ROM_d_2), .CLK(nclk), .OUT(TOS_HIGH_out[15:8]));
  tom_1_d_r D_REGISTER (
    .nENP(in_7), .nCCLR(in_18), .RCK(in_17), .R_nC(in_6), .nG(not_5_out), .nLOAD(in_16), .nENT(in_5),
    .U_nD(CTRL_p3[2]), .D(in_3), .CCK(npulse), .Q(D_REGISTER_q));
  tom_1_d_r R_REGISTER (
    .nENP(in_13), .nCCLR(in_18), .RCK(in_11), .R_nC(in_10), .nG(not_4_out), .nLOAD(in_12), .nENT(in_9),
    .U_nD(not_3_out), .D(in_8), .CCK(npulse), .Q(D_REGISTER_q));
  tom_1_is0 nTOS_eq__eq_0 (.\input (TOS_HIGH_out), .nis0(nTOS_eq__eq_0_nis0));
  // Probe TOS on TOS_HIGH_out
  LED led_5 (.in(nTOS_eq__eq_0_nis0));
  not not_7 (not_7_out, CTRL_p3[3]);
  // tom_1_io I_O_LOW: pin names not known; wires that end beside it: TOS_HIGH_out[7:0], not_7_out, I_O_LOW_p3
  // tom_1_io I_O_HIGH: pin names not known; wires that end beside it: TOS_HIGH_out[15:8], not_7_out, I_O_HIGH_p3
  // Probe stack addr on {in_4, D_REGISTER_q}
  RAMSinglePortSel #(.AddrBits(9), .Bits(16)) STACK (
    .A({in_4, D_REGISTER_q}), .CS(1'b1), .WE(CTRL_p3[3]), .OE(not_6_out), .D({I_O_HIGH_p3, I_O_LOW_p3}));
  // Probe stack_bus on {I_O_HIGH_p3, I_O_LOW_p3}
  tom_1_nand NAND (.A(TOS_HIGH_out), .B({I_O_HIGH_p3, I_O_LOW_p3}), .Vin(1'b1), .out(NAND_out));
  LED led_6 (.in(NAND_out[0]));
  LED led_7 (.in(NAND_out[1]));
  LED led_8 (.in(NAND_out[2]));
  LED led_9 (.in(NAND_out[3]));
  LED led_10 (.in(NAND_out[4]));
  LED led_11 (.in(NAND_out[5]));
  LED led_12 (.in(NAND_out[6]));
  LED led_13 (.in(NAND_out[7]));
  LED led_14 (.in(NAND_out[8]));
  LED led_15 (.in(NAND_out[9]));
  LED led_16 (.in(NAND_out[10]));
  LED led_17 (.in(NAND_out[11]));
  LED led_18 (.in(NAND_out[12]));
  LED led_19 (.in(NAND_out[13]));
  LED led_20 (.in(NAND_out[14]));
  LED led_21 (.in(NAND_out[15]));

  assign pulse = clk;

  // Other names for the same wires on the sheet: clk_t = clk_2; nreset = in_18

  // Notes on the sheet:
  //   in_6: default 1
  //   in_10: default 1
  //   in_12: default 1
  //   in_13: default 1
  //   in_16: default 1
  //   Clock
  //   contents of ROM (hex, n*v repeats v):
  //   9,ffff,9,eeee,15,0,80
  //   CTRL Pins
  //   0: D enable
  //   1: R enable
  //   2: D up/down / ~R up/down~
  //   3: STACK write enable + io enable / STACK output enable
  //   4: ADD enable
  //   5: NAND enable
  //   6: ROM_OUTPUT_ENABLE
  //   7: RAM enable
  //   8: pc load (break)
  //   Maybe a 2:1 decoder for ADD, NAND, ROM, and RAM?
  //   TOS
endmodule
